// Logisim project CS21B002_8bitALU_linux_version.circ as structural Verilog: 17 circuits, main circuit main
module main (
  input  in_1,
  input  [2:0] in_2,
  input  OUTPUT,
  input  in_4,
  input  in_5,
  input  in_6,
  input  in_7,
  output cout,
  output [7:0] Result
);

  wire bcd_to_7segment_new1_1_a, bcd_to_7segment_new1_1_b, bcd_to_7segment_new1_1_c,
       bcd_to_7segment_new1_1_d, bcd_to_7segment_new1_1_e, bcd_to_7segment_new1_1_f,
       bcd_to_7segment_new1_1_g, bcd_to_7segment_new1_2_a, bcd_to_7segment_new1_2_b,
       bcd_to_7segment_new1_2_c, bcd_to_7segment_new1_2_d, bcd_to_7segment_new1_2_e,
       bcd_to_7segment_new1_2_f, bcd_to_7segment_new1_2_g, bcd_to_7segment_new1_3_a,
       bcd_to_7segment_new1_3_b, bcd_to_7segment_new1_3_c, bcd_to_7segment_new1_3_d,
       bcd_to_7segment_new1_3_e, bcd_to_7segment_new1_3_f, bcd_to_7segment_new1_3_g,
       bcd_to_7segment_new1_4_a, bcd_to_7segment_new1_4_b, bcd_to_7segment_new1_4_c,
       bcd_to_7segment_new1_4_d, bcd_to_7segment_new1_4_e, bcd_to_7segment_new1_4_f,
       bcd_to_7segment_new1_4_g, bcd_to_7segment_new1_5_a, bcd_to_7segment_new1_5_b,
       bcd_to_7segment_new1_5_c, bcd_to_7segment_new1_5_d, bcd_to_7segment_new1_5_e,
       bcd_to_7segment_new1_5_f, bcd_to_7segment_new1_5_g, bcd_to_7segment_new1_6_a,
       bcd_to_7segment_new1_6_b, bcd_to_7segment_new1_6_c, bcd_to_7segment_new1_6_d,
       bcd_to_7segment_new1_6_e, bcd_to_7segment_new1_6_f, bcd_to_7segment_new1_6_g,
       bcd_to_7segment_new1_7_a, bcd_to_7segment_new1_7_b, bcd_to_7segment_new1_7_c,
       bcd_to_7segment_new1_7_d, bcd_to_7segment_new1_7_e, bcd_to_7segment_new1_7_f,
       bcd_to_7segment_new1_7_g, bcd_to_7segment_new1_8_a, bcd_to_7segment_new1_8_b,
       bcd_to_7segment_new1_8_c, bcd_to_7segment_new1_8_d, bcd_to_7segment_new1_8_e,
       bcd_to_7segment_new1_8_f, bcd_to_7segment_new1_8_g, bcd_to_7segment_new1_9_a,
       bcd_to_7segment_new1_9_b, bcd_to_7segment_new1_9_c, bcd_to_7segment_new1_9_d,
       bcd_to_7segment_new1_9_e, bcd_to_7segment_new1_9_f, bcd_to_7segment_new1_9_g, clock_1_out,
       clock_2_out, clock_3_out, dipswitch_1_p1, dipswitch_1_p2, dipswitch_1_p3, dipswitch_1_p4,
       dipswitch_1_p5, dipswitch_1_p6, dipswitch_1_p7, dipswitch_1_p8, dipswitch_2_p1, dipswitch_2_p2,
       dipswitch_2_p3, dipswitch_2_p4, dipswitch_2_p5, dipswitch_2_p6, dipswitch_2_p7, dipswitch_2_p8;
  wire [3:0] dda_algorithm_1_hundreds, dda_algorithm_1_ones, dda_algorithm_1_tens, dda_algorithm_2_hundreds,
       dda_algorithm_2_ones, dda_algorithm_2_tens, dda_algorithm_3_hundreds, dda_algorithm_3_ones,
       dda_algorithm_3_tens;
  wire [7:0] d_ff_1_q, d_ff_2_q, d_ff_17_q;

  BCD_TO_7SEGMENT_new1 bcd_to_7segment_new1_1 (
    .a3(dda_algorithm_1_hundreds[3]), .a2(dda_algorithm_1_hundreds[2]), .a1(dda_algorithm_1_hundreds[1]),
    .a12(dda_algorithm_1_hundreds[0]), .a(bcd_to_7segment_new1_1_a), .b(bcd_to_7segment_new1_1_b),
    .c(bcd_to_7segment_new1_1_c), .d(bcd_to_7segment_new1_1_d), .e(bcd_to_7segment_new1_1_e),
    .f(bcd_to_7segment_new1_1_f), .g(bcd_to_7segment_new1_1_g));
  Clock clock_1 (.out(clock_1_out));
  BCD_TO_7SEGMENT_new1 bcd_to_7segment_new1_2 (
    .a3(dda_algorithm_2_hundreds[3]), .a2(dda_algorithm_2_hundreds[2]), .a1(dda_algorithm_2_hundreds[1]),
    .a12(dda_algorithm_2_hundreds[0]), .a(bcd_to_7segment_new1_2_a), .b(bcd_to_7segment_new1_2_b),
    .c(bcd_to_7segment_new1_2_c), .d(bcd_to_7segment_new1_2_d), .e(bcd_to_7segment_new1_2_e),
    .f(bcd_to_7segment_new1_2_f), .g(bcd_to_7segment_new1_2_g));
  Clock clock_2 (.out(clock_2_out));
  _7_Segment_Display u_7_segment_display_1 (
    .g(bcd_to_7segment_new1_1_g), .f(bcd_to_7segment_new1_1_f), .a(bcd_to_7segment_new1_1_a),
    .b(bcd_to_7segment_new1_1_b), .e(bcd_to_7segment_new1_1_e), .d(bcd_to_7segment_new1_1_d),
    .c(bcd_to_7segment_new1_1_c));  // open: dp
  _7_Segment_Display u_7_segment_display_2 (
    .g(bcd_to_7segment_new1_2_g), .f(bcd_to_7segment_new1_2_f), .a(bcd_to_7segment_new1_2_a),
    .b(bcd_to_7segment_new1_2_b), .e(bcd_to_7segment_new1_2_e), .d(bcd_to_7segment_new1_2_d),
    .c(bcd_to_7segment_new1_2_c));  // open: dp
  BCD_TO_7SEGMENT_new1 bcd_to_7segment_new1_3 (
    .a3(dda_algorithm_1_tens[3]), .a2(dda_algorithm_1_tens[2]), .a1(dda_algorithm_1_tens[1]),
    .a12(dda_algorithm_1_tens[0]), .a(bcd_to_7segment_new1_3_a), .b(bcd_to_7segment_new1_3_b),
    .c(bcd_to_7segment_new1_3_c), .d(bcd_to_7segment_new1_3_d), .e(bcd_to_7segment_new1_3_e),
    .f(bcd_to_7segment_new1_3_f), .g(bcd_to_7segment_new1_3_g));
  DDA_ALGORITHM dda_algorithm_1 (
    .\input (d_ff_2_q), .hundreds(dda_algorithm_1_hundreds), .tens(dda_algorithm_1_tens),
    .ones(dda_algorithm_1_ones));
  D_Flip_Flop d_ff_1 (.clk(clock_1_out), .D(dipswitch_2_p1), .Q(d_ff_1_q[0]), .reset(in_1));  // open: Qn, preset
  BCD_TO_7SEGMENT_new1 bcd_to_7segment_new1_4 (
    .a3(dda_algorithm_2_tens[3]), .a2(dda_algorithm_2_tens[2]), .a1(dda_algorithm_2_tens[1]),
    .a12(dda_algorithm_2_tens[0]), .a(bcd_to_7segment_new1_4_a), .b(bcd_to_7segment_new1_4_b),
    .c(bcd_to_7segment_new1_4_c), .d(bcd_to_7segment_new1_4_d), .e(bcd_to_7segment_new1_4_e),
    .f(bcd_to_7segment_new1_4_f), .g(bcd_to_7segment_new1_4_g));
  DDA_ALGORITHM dda_algorithm_2 (
    .\input (d_ff_1_q), .hundreds(dda_algorithm_2_hundreds), .tens(dda_algorithm_2_tens),
    .ones(dda_algorithm_2_ones));
  D_Flip_Flop d_ff_2 (.clk(clock_2_out), .D(dipswitch_1_p1), .Q(d_ff_2_q[0]), .reset(in_7));  // open: Qn, preset
  _7_Segment_Display u_7_segment_display_3 (
    .g(bcd_to_7segment_new1_3_g), .f(bcd_to_7segment_new1_3_f), .a(bcd_to_7segment_new1_3_a),
    .b(bcd_to_7segment_new1_3_b), .e(bcd_to_7segment_new1_3_e), .d(bcd_to_7segment_new1_3_d),
    .c(bcd_to_7segment_new1_3_c));  // open: dp
  D_Flip_Flop d_ff_3 (.clk(clock_1_out), .D(dipswitch_2_p2), .Q(d_ff_1_q[1]), .reset(in_1));  // open: Qn, preset
  _7_Segment_Display u_7_segment_display_4 (
    .g(bcd_to_7segment_new1_4_g), .f(bcd_to_7segment_new1_4_f), .a(bcd_to_7segment_new1_4_a),
    .b(bcd_to_7segment_new1_4_b), .e(bcd_to_7segment_new1_4_e), .d(bcd_to_7segment_new1_4_d),
    .c(bcd_to_7segment_new1_4_c));  // open: dp
  D_Flip_Flop d_ff_4 (.clk(clock_2_out), .D(dipswitch_1_p2), .Q(d_ff_2_q[1]), .reset(in_7));  // open: Qn, preset
  BCD_TO_7SEGMENT_new1 bcd_to_7segment_new1_5 (
    .a3(dda_algorithm_1_ones[3]), .a2(dda_algorithm_1_ones[2]), .a1(dda_algorithm_1_ones[1]),
    .a12(dda_algorithm_1_ones[0]), .a(bcd_to_7segment_new1_5_a), .b(bcd_to_7segment_new1_5_b),
    .c(bcd_to_7segment_new1_5_c), .d(bcd_to_7segment_new1_5_d), .e(bcd_to_7segment_new1_5_e),
    .f(bcd_to_7segment_new1_5_f), .g(bcd_to_7segment_new1_5_g));
  D_Flip_Flop d_ff_5 (.clk(clock_1_out), .D(dipswitch_2_p3), .Q(d_ff_1_q[2]), .reset(in_1));  // open: Qn, preset
  BCD_TO_7SEGMENT_new1 bcd_to_7segment_new1_6 (
    .a3(dda_algorithm_2_ones[3]), .a2(dda_algorithm_2_ones[2]), .a1(dda_algorithm_2_ones[1]),
    .a12(dda_algorithm_2_ones[0]), .a(bcd_to_7segment_new1_6_a), .b(bcd_to_7segment_new1_6_b),
    .c(bcd_to_7segment_new1_6_c), .d(bcd_to_7segment_new1_6_d), .e(bcd_to_7segment_new1_6_e),
    .f(bcd_to_7segment_new1_6_f), .g(bcd_to_7segment_new1_6_g));
  D_Flip_Flop d_ff_6 (.clk(clock_2_out), .D(dipswitch_1_p3), .Q(d_ff_2_q[2]), .reset(in_7));  // open: Qn, preset
  _7_Segment_Display u_7_segment_display_5 (
    .g(bcd_to_7segment_new1_5_g), .f(bcd_to_7segment_new1_5_f), .a(bcd_to_7segment_new1_5_a),
    .b(bcd_to_7segment_new1_5_b), .e(bcd_to_7segment_new1_5_e), .d(bcd_to_7segment_new1_5_d),
    .c(bcd_to_7segment_new1_5_c));  // open: dp
  _7_Segment_Display u_7_segment_display_6 (
    .g(bcd_to_7segment_new1_6_g), .f(bcd_to_7segment_new1_6_f), .a(bcd_to_7segment_new1_6_a),
    .b(bcd_to_7segment_new1_6_b), .e(bcd_to_7segment_new1_6_e), .d(bcd_to_7segment_new1_6_d),
    .c(bcd_to_7segment_new1_6_c));  // open: dp
  D_Flip_Flop d_ff_7 (.clk(clock_2_out), .D(dipswitch_1_p4), .Q(d_ff_2_q[3]), .reset(in_7));  // open: Qn, preset
  D_Flip_Flop d_ff_8 (.clk(clock_1_out), .D(dipswitch_2_p4), .Q(d_ff_1_q[3]), .reset(in_1));  // open: Qn, preset
  // DipSwitch #(.NSwitches(8)) dipswitch_1: pin names not known; wires that end beside it: dipswitch_1_p1, dipswitch_1_p2, dipswitch_1_p3, dipswitch_1_p4, dipswitch_1_p5, dipswitch_1_p6, dipswitch_1_p7, dipswitch_1_p8
  // DipSwitch #(.NSwitches(8)) dipswitch_2: pin names not known; wires that end beside it: dipswitch_2_p1, dipswitch_2_p2, dipswitch_2_p3, dipswitch_2_p4, dipswitch_2_p5, dipswitch_2_p6, dipswitch_2_p7, dipswitch_2_p8
  D_Flip_Flop d_ff_9 (.clk(clock_2_out), .D(dipswitch_1_p5), .Q(d_ff_2_q[4]), .reset(in_7));  // open: Qn, preset
  D_Flip_Flop d_ff_10 (.clk(clock_1_out), .D(dipswitch_2_p5), .Q(d_ff_1_q[4]), .reset(in_1));  // open: Qn, preset
  D_Flip_Flop d_ff_11 (.clk(clock_1_out), .D(dipswitch_2_p6), .Q(d_ff_1_q[5]), .reset(in_1));  // open: Qn, preset
  D_Flip_Flop d_ff_12 (.clk(clock_2_out), .D(dipswitch_1_p6), .Q(d_ff_2_q[5]), .reset(in_7));  // open: Qn, preset
  D_Flip_Flop d_ff_13 (.clk(clock_1_out), .D(dipswitch_2_p7), .Q(d_ff_1_q[6]), .reset(in_1));  // open: Qn, preset
  D_Flip_Flop d_ff_14 (.clk(clock_2_out), .D(dipswitch_1_p7), .Q(d_ff_2_q[6]), .reset(in_7));  // open: Qn, preset
  D_Flip_Flop d_ff_15 (.clk(clock_1_out), .D(dipswitch_2_p8), .Q(d_ff_1_q[7]), .reset(in_1));  // open: Qn, preset
  _8bit_ALU u_8bit_alu_1 (
    .A(d_ff_1_q), .B(d_ff_2_q), .cout(cout), .OUTPUT(Result), .Transfer(in_4), .sub(in_5), .cin(in_6),
    .S0(in_2[0]), .S1(in_2[1]), .S2(in_2[2]));
  D_Flip_Flop d_ff_16 (.clk(clock_2_out), .D(dipswitch_1_p8), .Q(d_ff_2_q[7]), .reset(in_7));  // open: Qn, preset
  Clock clock_3 (.out(clock_3_out));
  BCD_TO_7SEGMENT_new1 bcd_to_7segment_new1_7 (
    .a3(dda_algorithm_3_hundreds[3]), .a2(dda_algorithm_3_hundreds[2]), .a1(dda_algorithm_3_hundreds[1]),
    .a12(dda_algorithm_3_hundreds[0]), .a(bcd_to_7segment_new1_7_a), .b(bcd_to_7segment_new1_7_b),
    .c(bcd_to_7segment_new1_7_c), .d(bcd_to_7segment_new1_7_d), .e(bcd_to_7segment_new1_7_e),
    .f(bcd_to_7segment_new1_7_f), .g(bcd_to_7segment_new1_7_g));
  D_Flip_Flop d_ff_17 (.clk(clock_3_out), .D(Result[0]), .Q(d_ff_17_q[0]), .reset(OUTPUT));  // open: Qn, preset
  _7_Segment_Display u_7_segment_display_7 (
    .g(bcd_to_7segment_new1_7_g), .f(bcd_to_7segment_new1_7_f), .a(bcd_to_7segment_new1_7_a),
    .b(bcd_to_7segment_new1_7_b), .e(bcd_to_7segment_new1_7_e), .d(bcd_to_7segment_new1_7_d),
    .c(bcd_to_7segment_new1_7_c));  // open: dp
  D_Flip_Flop d_ff_18 (.clk(clock_3_out), .D(Result[1]), .Q(d_ff_17_q[1]), .reset(OUTPUT));  // open: Qn, preset
  BCD_TO_7SEGMENT_new1 bcd_to_7segment_new1_8 (
    .a3(dda_algorithm_3_tens[3]), .a2(dda_algorithm_3_tens[2]), .a1(dda_algorithm_3_tens[1]),
    .a12(dda_algorithm_3_tens[0]), .a(bcd_to_7segment_new1_8_a), .b(bcd_to_7segment_new1_8_b),
    .c(bcd_to_7segment_new1_8_c), .d(bcd_to_7segment_new1_8_d), .e(bcd_to_7segment_new1_8_e),
    .f(bcd_to_7segment_new1_8_f), .g(bcd_to_7segment_new1_8_g));
  DDA_ALGORITHM dda_algorithm_3 (
    .\input (d_ff_17_q), .hundreds(dda_algorithm_3_hundreds), .tens(dda_algorithm_3_tens),
    .ones(dda_algorithm_3_ones));
  D_Flip_Flop d_ff_19 (.clk(clock_3_out), .D(Result[2]), .Q(d_ff_17_q[2]), .reset(OUTPUT));  // open: Qn, preset
  _7_Segment_Display u_7_segment_display_8 (
    .g(bcd_to_7segment_new1_8_g), .f(bcd_to_7segment_new1_8_f), .a(bcd_to_7segment_new1_8_a),
    .b(bcd_to_7segment_new1_8_b), .e(bcd_to_7segment_new1_8_e), .d(bcd_to_7segment_new1_8_d),
    .c(bcd_to_7segment_new1_8_c));  // open: dp
  D_Flip_Flop d_ff_20 (.clk(clock_3_out), .D(Result[3]), .Q(d_ff_17_q[3]), .reset(OUTPUT));  // open: Qn, preset
  BCD_TO_7SEGMENT_new1 bcd_to_7segment_new1_9 (
    .a3(dda_algorithm_3_ones[3]), .a2(dda_algorithm_3_ones[2]), .a1(dda_algorithm_3_ones[1]),
    .a12(dda_algorithm_3_ones[0]), .a(bcd_to_7segment_new1_9_a), .b(bcd_to_7segment_new1_9_b),
    .c(bcd_to_7segment_new1_9_c), .d(bcd_to_7segment_new1_9_d), .e(bcd_to_7segment_new1_9_e),
    .f(bcd_to_7segment_new1_9_f), .g(bcd_to_7segment_new1_9_g));
  D_Flip_Flop d_ff_21 (.clk(clock_3_out), .D(Result[4]), .Q(d_ff_17_q[4]), .reset(OUTPUT));  // open: Qn, preset
  _7_Segment_Display u_7_segment_display_9 (
    .g(bcd_to_7segment_new1_9_g), .f(bcd_to_7segment_new1_9_f), .a(bcd_to_7segment_new1_9_a),
    .b(bcd_to_7segment_new1_9_b), .e(bcd_to_7segment_new1_9_e), .d(bcd_to_7segment_new1_9_d),
    .c(bcd_to_7segment_new1_9_c));  // open: dp
  D_Flip_Flop d_ff_22 (.clk(clock_3_out), .D(Result[5]), .Q(d_ff_17_q[5]), .reset(OUTPUT));  // open: Qn, preset
  D_Flip_Flop d_ff_23 (.clk(clock_3_out), .D(Result[6]), .Q(d_ff_17_q[6]), .reset(OUTPUT));  // open: Qn, preset
  D_Flip_Flop d_ff_24 (.clk(clock_3_out), .D(Result[7]), .Q(d_ff_17_q[7]), .reset(OUTPUT));  // open: Qn, preset

  // Notes on the sheet:
  //   INPUT A
  //   INPUT B
endmodule

module _8bit_multiplier (
  input  A0,
  input  A4,
  input  A3,
  input  A6,
  input  A5,
  input  A2,
  input  A1,
  input  A7,
  input  B0,
  input  B1,
  input  B2,
  input  B3,
  input  B4,
  input  B5,
  input  B6,
  input  B7,
  output M0,
  output M1,
  output M2,
  output M3,
  output M4,
  output M5,
  output M6,
  output M7
);

  wire and_1_out, and_2_out, and_3_out, and_4_out, and_5_out, and_6_out, and_7_out, and_8_out, and_9_out,
       and_10_out, and_11_out, and_12_out, and_13_out, and_14_out, and_15_out, and_16_out, and_17_out,
       and_18_out, and_19_out, and_20_out, and_21_out, and_22_out, and_23_out, and_24_out, and_25_out,
       and_26_out, and_27_out, and_28_out, and_29_out, and_30_out, and_31_out, and_32_out, and_33_out,
       and_34_out, and_35_out, and_36_out, and_37_out, and_38_out, and_39_out, and_40_out, and_41_out,
       and_42_out, and_43_out, and_44_out, and_45_out, and_46_out, and_47_out, and_48_out, and_49_out,
       and_50_out, and_51_out, and_52_out, and_53_out, and_54_out, and_55_out, and_56_out, and_57_out,
       and_58_out, and_59_out, and_60_out, and_61_out, and_62_out, and_63_out, n8bit_full_adder_2_cout,
       n8bit_full_adder_2_s1, n8bit_full_adder_2_s2, n8bit_full_adder_2_s3, n8bit_full_adder_2_s4,
       n8bit_full_adder_2_s5, n8bit_full_adder_2_s6, n8bit_full_adder_2_s7, n8bit_full_adder_3_cout,
       n8bit_full_adder_3_s1, n8bit_full_adder_3_s2, n8bit_full_adder_3_s3, n8bit_full_adder_3_s4,
       n8bit_full_adder_3_s5, n8bit_full_adder_3_s6, n8bit_full_adder_3_s7, n8bit_full_adder_4_cout,
       n8bit_full_adder_4_s1, n8bit_full_adder_4_s2, n8bit_full_adder_4_s3, n8bit_full_adder_4_s4,
       n8bit_full_adder_4_s5, n8bit_full_adder_4_s6, n8bit_full_adder_4_s7, n8bit_full_adder_5_cout,
       n8bit_full_adder_5_s1, n8bit_full_adder_5_s2, n8bit_full_adder_5_s3, n8bit_full_adder_5_s4,
       n8bit_full_adder_5_s5, n8bit_full_adder_5_s6, n8bit_full_adder_5_s7, n8bit_full_adder_6_cout,
       n8bit_full_adder_6_s1, n8bit_full_adder_6_s2, n8bit_full_adder_6_s3, n8bit_full_adder_6_s4,
       n8bit_full_adder_6_s5, n8bit_full_adder_6_s6, n8bit_full_adder_6_s7, n8bit_full_adder_7_cout,
       n8bit_full_adder_7_s1, n8bit_full_adder_7_s2, n8bit_full_adder_7_s3, n8bit_full_adder_7_s4,
       n8bit_full_adder_7_s5, n8bit_full_adder_7_s6, n8bit_full_adder_7_s7;

  and and_1 (and_1_out, B7, A7);
  and and_2 (and_2_out, B7, A4);
  and and_3 (and_3_out, B7, A5);
  and and_4 (and_4_out, B7, A6);
  and and_5 (and_5_out, B7, A3);
  and and_6 (and_6_out, B7, A2);
  and and_7 (and_7_out, B7, A1);
  and and_8 (and_8_out, B7, A0);
  _8bit_full_adder u_8bit_full_adder_1 (
    .A2(n8bit_full_adder_2_s3), .A0(n8bit_full_adder_2_s1), .A1(n8bit_full_adder_2_s2), .B2(and_6_out),
    .B0(and_8_out), .B1(and_7_out), .A3(n8bit_full_adder_2_s4), .A4(n8bit_full_adder_2_s5),
    .A5(n8bit_full_adder_2_s6), .A6(n8bit_full_adder_2_s7), .A7(n8bit_full_adder_2_cout), .B3(and_5_out),
    .B4(and_2_out), .B5(and_3_out), .B6(and_4_out), .B7(and_1_out), .S0(M7), .cin(1'b0));  // open: COUT, S7, S5, S6, S1, S2, S3, S4
  and and_9 (and_9_out, B6, A6);
  and and_10 (and_10_out, B6, A7);
  and and_11 (and_11_out, B6, A5);
  and and_12 (and_12_out, B6, A3);
  and and_13 (and_13_out, B6, A4);
  and and_14 (and_14_out, B6, A2);
  and and_15 (and_15_out, B6, A1);
  and and_16 (and_16_out, B6, A0);
  _8bit_full_adder u_8bit_full_adder_2 (
    .A2(n8bit_full_adder_3_s3), .A0(n8bit_full_adder_3_s1), .A1(n8bit_full_adder_3_s2), .B2(and_14_out),
    .B0(and_16_out), .B1(and_15_out), .A3(n8bit_full_adder_3_s4), .A4(n8bit_full_adder_3_s5),
    .A5(n8bit_full_adder_3_s6), .A6(n8bit_full_adder_3_s7), .A7(n8bit_full_adder_3_cout), .B3(and_12_out),
    .B4(and_13_out), .B5(and_11_out), .B6(and_9_out), .B7(and_10_out), .COUT(n8bit_full_adder_2_cout),
    .S7(n8bit_full_adder_2_s7), .S5(n8bit_full_adder_2_s5), .S6(n8bit_full_adder_2_s6), .S0(M6),
    .S1(n8bit_full_adder_2_s1), .S2(n8bit_full_adder_2_s2), .S3(n8bit_full_adder_2_s3),
    .S4(n8bit_full_adder_2_s4), .cin(1'b0));
  and and_17 (and_17_out, B5, A5);
  and and_18 (and_18_out, B5, A6);
  and and_19 (and_19_out, B5, A7);
  and and_20 (and_20_out, B5, A4);
  and and_21 (and_21_out, B5, A3);
  and and_22 (and_22_out, B5, A0);
  and and_23 (and_23_out, B5, A1);
  and and_24 (and_24_out, B5, A2);
  _8bit_full_adder u_8bit_full_adder_3 (
    .A2(n8bit_full_adder_4_s3), .A0(n8bit_full_adder_4_s1), .A1(n8bit_full_adder_4_s2), .B2(and_24_out),
    .B0(and_22_out), .B1(and_23_out), .A3(n8bit_full_adder_4_s4), .A4(n8bit_full_adder_4_s5),
    .A5(n8bit_full_adder_4_s6), .A6(n8bit_full_adder_4_s7), .A7(n8bit_full_adder_4_cout), .B3(and_21_out),
    .B4(and_20_out), .B5(and_17_out), .B6(and_18_out), .B7(and_19_out), .COUT(n8bit_full_adder_3_cout),
    .S7(n8bit_full_adder_3_s7), .S5(n8bit_full_adder_3_s5), .S6(n8bit_full_adder_3_s6), .S0(M5),
    .S1(n8bit_full_adder_3_s1), .S2(n8bit_full_adder_3_s2), .S3(n8bit_full_adder_3_s3),
    .S4(n8bit_full_adder_3_s4), .cin(1'b0));
  and and_25 (and_25_out, B4, A7);
  and and_26 (and_26_out, B4, A5);
  and and_27 (and_27_out, B4, A6);
  and and_28 (and_28_out, B0, A7);
  and and_29 (and_29_out, B4, A4);
  and and_30 (and_30_out, B4, A2);
  and and_31 (and_31_out, B4, A3);
  and and_32 (and_32_out, B4, A0);
  and and_33 (and_33_out, B4, A1);
  and and_34 (and_34_out, B0, A6);
  and and_35 (and_35_out, B3, A7);
  _8bit_full_adder u_8bit_full_adder_4 (
    .A2(n8bit_full_adder_5_s3), .A0(n8bit_full_adder_5_s1), .A1(n8bit_full_adder_5_s2), .B2(and_30_out),
    .B0(and_32_out), .B1(and_33_out), .A3(n8bit_full_adder_5_s4), .A4(n8bit_full_adder_5_s5),
    .A5(n8bit_full_adder_5_s6), .A6(n8bit_full_adder_5_s7), .A7(n8bit_full_adder_5_cout), .B3(and_31_out),
    .B4(and_29_out), .B5(and_26_out), .B6(and_27_out), .B7(and_25_out), .COUT(n8bit_full_adder_4_cout),
    .S7(n8bit_full_adder_4_s7), .S5(n8bit_full_adder_4_s5), .S6(n8bit_full_adder_4_s6), .S0(M4),
    .S1(n8bit_full_adder_4_s1), .S2(n8bit_full_adder_4_s2), .S3(n8bit_full_adder_4_s3),
    .S4(n8bit_full_adder_4_s4), .cin(1'b0));
  and and_36 (and_36_out, B3, A6);
  and and_37 (and_37_out, B3, A5);
  and and_38 (and_38_out, B3, A3);
  and and_39 (and_39_out, B3, A2);
  and and_40 (and_40_out, B3, A4);
  and and_41 (and_41_out, B0, A5);
  and and_42 (and_42_out, B3, A1);
  and and_43 (and_43_out, B3, A0);
  _8bit_full_adder u_8bit_full_adder_5 (
    .A2(n8bit_full_adder_6_s3), .A0(n8bit_full_adder_6_s1), .A1(n8bit_full_adder_6_s2), .B2(and_39_out),
    .B0(and_43_out), .B1(and_42_out), .A3(n8bit_full_adder_6_s4), .A4(n8bit_full_adder_6_s5),
    .A5(n8bit_full_adder_6_s6), .A6(n8bit_full_adder_6_s7), .A7(n8bit_full_adder_6_cout), .B3(and_38_out),
    .B4(and_40_out), .B5(and_37_out), .B6(and_36_out), .B7(and_35_out), .COUT(n8bit_full_adder_5_cout),
    .S7(n8bit_full_adder_5_s7), .S5(n8bit_full_adder_5_s5), .S6(n8bit_full_adder_5_s6), .S0(M3),
    .S1(n8bit_full_adder_5_s1), .S2(n8bit_full_adder_5_s2), .S3(n8bit_full_adder_5_s3),
    .S4(n8bit_full_adder_5_s4), .cin(1'b0));
  and and_44 (and_44_out, B0, A4);
  and and_45 (and_45_out, B2, A5);
  and and_46 (and_46_out, B2, A6);
  and and_47 (and_47_out, B2, A7);
  and and_48 (and_48_out, B2, A3);
  and and_49 (and_49_out, B2, A2);
  and and_50 (and_50_out, B2, A4);
  and and_51 (and_51_out, B2, A1);
  and and_52 (and_52_out, B2, A0);
  and and_53 (and_53_out, B0, A3);
  and and_54 (and_54_out, B1, A7);
  _8bit_full_adder u_8bit_full_adder_6 (
    .A2(n8bit_full_adder_7_s3), .A0(n8bit_full_adder_7_s1), .A1(n8bit_full_adder_7_s2), .B2(and_49_out),
    .B0(and_52_out), .B1(and_51_out), .A3(n8bit_full_adder_7_s4), .A4(n8bit_full_adder_7_s5),
    .A5(n8bit_full_adder_7_s6), .A6(n8bit_full_adder_7_s7), .A7(n8bit_full_adder_7_cout), .B3(and_48_out),
    .B4(and_50_out), .B5(and_45_out), .B6(and_46_out), .B7(and_47_out), .COUT(n8bit_full_adder_6_cout),
    .S7(n8bit_full_adder_6_s7), .S5(n8bit_full_adder_6_s5), .S6(n8bit_full_adder_6_s6), .S0(M2),
    .S1(n8bit_full_adder_6_s1), .S2(n8bit_full_adder_6_s2), .S3(n8bit_full_adder_6_s3),
    .S4(n8bit_full_adder_6_s4), .cin(1'b0));
  and and_55 (and_55_out, B0, A2);
  and and_56 (and_56_out, B1, A6);
  and and_57 (and_57_out, B1, A5);
  and and_58 (and_58_out, B1, A2);
  and and_59 (and_59_out, B1, A3);
  and and_60 (and_60_out, B1, A4);
  and and_61 (and_61_out, B1, A0);
  and and_62 (and_62_out, B1, A1);
  and and_63 (and_63_out, B0, A1);
  _8bit_full_adder u_8bit_full_adder_7 (
    .A2(and_53_out), .A0(and_63_out), .A1(and_55_out), .B2(and_58_out), .B0(and_61_out), .B1(and_62_out),
    .A3(and_44_out), .A4(and_41_out), .A5(and_34_out), .A6(and_28_out), .A7(1'b0), .B3(and_59_out),
    .B4(and_60_out), .B5(and_57_out), .B6(and_56_out), .B7(and_54_out), .COUT(n8bit_full_adder_7_cout),
    .S7(n8bit_full_adder_7_s7), .S5(n8bit_full_adder_7_s5), .S6(n8bit_full_adder_7_s6), .S0(M1),
    .S1(n8bit_full_adder_7_s1), .S2(n8bit_full_adder_7_s2), .S3(n8bit_full_adder_7_s3),
    .S4(n8bit_full_adder_7_s4), .cin(1'b0));
  and and_64 (M0, B0, A0);
endmodule

module _8bit_full_adder (
  input  A2,
  input  A3,
  input  A4,
  input  A5,
  input  A6,
  input  A7,
  input  A0,
  input  A1,
  input  B2,
  input  B3,
  input  B4,
  input  B5,
  input  B6,
  input  B7,
  input  B0,
  input  B1,
  input  cin,
  output COUT,
  output S7,
  output S5,
  output S6,
  output S0,
  output S1,
  output S2,
  output S3,
  output S4
);

  wire n1bit_full_adder_1_cout, n1bit_full_adder_2_cout, n1bit_full_adder_3_cout, n1bit_full_adder_4_cout,
       n1bit_full_adder_5_cout, n1bit_full_adder_6_cout, n1bit_full_adder_7_cout;

  _1bit_full_adder u_1bit_full_adder_1 (.A(A0), .B(B0), .cin(cin), .sum(S0), .cout(n1bit_full_adder_1_cout));
  _1bit_full_adder u_1bit_full_adder_2 (
    .A(A1), .B(B1), .cin(n1bit_full_adder_1_cout), .sum(S1), .cout(n1bit_full_adder_2_cout));
  _1bit_full_adder u_1bit_full_adder_3 (
    .A(A2), .B(B2), .cin(n1bit_full_adder_2_cout), .sum(S2), .cout(n1bit_full_adder_3_cout));
  _1bit_full_adder u_1bit_full_adder_4 (
    .A(A3), .B(B3), .cin(n1bit_full_adder_3_cout), .sum(S3), .cout(n1bit_full_adder_4_cout));
  _1bit_full_adder u_1bit_full_adder_5 (
    .A(A4), .B(B4), .cin(n1bit_full_adder_4_cout), .sum(S4), .cout(n1bit_full_adder_5_cout));
  _1bit_full_adder u_1bit_full_adder_6 (
    .A(A5), .B(B5), .cin(n1bit_full_adder_5_cout), .sum(S5), .cout(n1bit_full_adder_6_cout));
  _1bit_full_adder u_1bit_full_adder_7 (
    .A(A6), .B(B6), .cin(n1bit_full_adder_6_cout), .sum(S6), .cout(n1bit_full_adder_7_cout));
  _1bit_full_adder u_1bit_full_adder_8 (.A(A7), .B(B7), .cin(n1bit_full_adder_7_cout), .sum(S7), .cout(COUT));
endmodule

module _1bit_full_adder (
  input  A,
  input  B,
  input  cin,
  output sum,
  output cout
);

  wire and_1_out, and_2_out, xor_1_out;

  xor xor_1 (xor_1_out, A, B);
  and and_1 (and_1_out, B, A);
  xor xor_2 (sum, xor_1_out, cin);
  and and_2 (and_2_out, xor_1_out, cin);
  or or_1 (cout, and_1_out, and_2_out);
endmodule

module \new  (
  input  [7:0] in_1,
  input  [7:0] in_2,
  output [7:0] M7,
  output [7:0] M7_2,
  output [7:0] M7_3
);

  _8bit_multiplier u_8bit_multiplier_1 (
    .B0(in_2[0]), .B1(in_2[1]), .B2(in_2[2]), .B3(in_2[3]), .B4(in_2[4]), .B5(in_2[5]), .B6(in_2[6]),
    .B7(in_2[7]), .M1(M7[1]), .M2(M7[2]), .M3(M7[3]), .M0(M7[0]), .M4(M7[4]), .M5(M7[5]), .M6(M7[6]),
    .M7(M7[7]), .A7(in_1[7]), .A6(in_1[6]), .A5(in_1[5]), .A4(in_1[4]), .A3(in_1[3]), .A2(in_1[2]),
    .A1(in_1[1]), .A0(in_1[0]));
  Multiplier multiplier_1 (.a(in_1), .b(in_2), .out(M7_3));  // open: cin, cout
  assign M7_2 = M7 ^ M7_3;  // XOR_Gate xor_1, 8 bits wide
endmodule

module _8bit_ALU (
  input  Transfer,
  input  sub,
  input  [7:0] A,
  input  [7:0] B,
  input  cin,
  input  S0,
  input  S1,
  input  S2,
  output cout,
  output [7:0] OUTPUT
);

  wire and_1_out, and_2_out, and_3_out, and_4_out, and_5_out, and_6_out, and_7_out, and_8_out, not_1_out,
       xor_1_out, xor_2_out, xor_3_out, xor_4_out, xor_5_out, xor_6_out, xor_7_out, xor_8_out;
  wire [7:0] n8bit_full_adder_1_s0, n8bit_multiplier_1_m0, n8bitwiseand_1_n0, n8bitwisenand_1_n0,
       n8bitwisenor_1_n0, n8bitwiseor_1_n0, n8bitwisexnor_1_n0, n8bitwisexor_1_n0;

  not not_1 (not_1_out, Transfer);
  and and_1 (and_1_out, B[0], not_1_out);
  and and_2 (and_2_out, B[1], not_1_out);
  and and_3 (and_3_out, B[2], not_1_out);
  and and_4 (and_4_out, B[3], not_1_out);
  and and_5 (and_5_out, B[4], not_1_out);
  and and_6 (and_6_out, B[5], not_1_out);
  and and_7 (and_7_out, B[6], not_1_out);
  and and_8 (and_8_out, B[7], not_1_out);
  _8bit_multiplier u_8bit_multiplier_1 (
    .B0(B[0]), .B1(B[1]), .B2(B[2]), .B3(B[3]), .B4(B[4]), .B5(B[5]), .B6(B[6]), .B7(B[7]),
    .M1(n8bit_multiplier_1_m0[1]), .M2(n8bit_multiplier_1_m0[2]), .M3(n8bit_multiplier_1_m0[3]),
    .M0(n8bit_multiplier_1_m0[0]), .M4(n8bit_multiplier_1_m0[4]), .M5(n8bit_multiplier_1_m0[5]),
    .M6(n8bit_multiplier_1_m0[6]), .M7(n8bit_multiplier_1_m0[7]), .A7(A[7]), .A6(A[6]), .A5(A[5]), .A4(A[4]),
    .A3(A[3]), .A2(A[2]), .A1(A[1]), .A0(A[0]));
  _8bitwiseAND u_8bitwiseand_1 (
    .A0(A[0]), .B0(B[0]), .A1(A[1]), .B1(B[1]), .A2(A[2]), .B2(B[2]), .A3(A[3]), .B3(B[3]), .A4(A[4]),
    .B4(B[4]), .A5(A[5]), .B5(B[5]), .A6(A[6]), .B6(B[6]), .A7(A[7]), .B7(B[7]), .N0(n8bitwiseand_1_n0[0]),
    .N1(n8bitwiseand_1_n0[1]), .N2(n8bitwiseand_1_n0[2]), .N3(n8bitwiseand_1_n0[3]),
    .N4(n8bitwiseand_1_n0[4]), .N5(n8bitwiseand_1_n0[5]), .N6(n8bitwiseand_1_n0[6]), .N7(n8bitwiseand_1_n0[7]));
  _8bitwiseNAND u_8bitwisenand_1 (
    .A0(A[0]), .B0(B[0]), .A1(A[1]), .B1(B[1]), .A2(A[2]), .B2(B[2]), .A3(A[3]), .B3(B[3]), .A4(A[4]),
    .B4(B[4]), .A5(A[5]), .B5(B[5]), .A6(A[6]), .B6(B[6]), .A7(A[7]), .B7(B[7]), .N0(n8bitwisenand_1_n0[0]),
    .N1(n8bitwisenand_1_n0[1]), .N2(n8bitwisenand_1_n0[2]), .N3(n8bitwisenand_1_n0[3]),
    .N4(n8bitwisenand_1_n0[4]), .N5(n8bitwisenand_1_n0[5]), .N6(n8bitwisenand_1_n0[6]),
    .N7(n8bitwisenand_1_n0[7]));
  _8bitwiseOR u_8bitwiseor_1 (
    .A0(A[0]), .B0(B[0]), .A1(A[1]), .B1(B[1]), .A2(A[2]), .B2(B[2]), .A3(A[3]), .B3(B[3]), .A4(A[4]),
    .B4(B[4]), .A5(A[5]), .B5(B[5]), .A6(A[6]), .B6(B[6]), .A7(A[7]), .B7(B[7]), .N0(n8bitwiseor_1_n0[0]),
    .N1(n8bitwiseor_1_n0[1]), .N2(n8bitwiseor_1_n0[2]), .N3(n8bitwiseor_1_n0[3]), .N4(n8bitwiseor_1_n0[4]),
    .N5(n8bitwiseor_1_n0[5]), .N6(n8bitwiseor_1_n0[6]), .N7(n8bitwiseor_1_n0[7]));
  _8bitwiseNOR u_8bitwisenor_1 (
    .A0(A[0]), .B0(B[0]), .A1(A[1]), .B1(B[1]), .A2(A[2]), .B2(B[2]), .A3(A[3]), .B3(B[3]), .A4(A[4]),
    .B4(B[4]), .A5(A[5]), .B5(B[5]), .A6(A[6]), .B6(B[6]), .A7(A[7]), .B7(B[7]), .N0(n8bitwisenor_1_n0[0]),
    .N1(n8bitwisenor_1_n0[1]), .N2(n8bitwisenor_1_n0[2]), .N3(n8bitwisenor_1_n0[3]),
    .N4(n8bitwisenor_1_n0[4]), .N5(n8bitwisenor_1_n0[5]), .N6(n8bitwisenor_1_n0[6]), .N7(n8bitwisenor_1_n0[7]));
  _8bitwiseXOR u_8bitwisexor_1 (
    .A0(A[0]), .B0(B[0]), .A1(A[1]), .B1(B[1]), .A2(A[2]), .B2(B[2]), .A3(A[3]), .B3(B[3]), .A4(A[4]),
    .B4(B[4]), .A5(A[5]), .B5(B[5]), .A6(A[6]), .B6(B[6]), .A7(A[7]), .B7(B[7]), .N0(n8bitwisexor_1_n0[0]),
    .N1(n8bitwisexor_1_n0[1]), .N2(n8bitwisexor_1_n0[2]), .N3(n8bitwisexor_1_n0[3]),
    .N4(n8bitwisexor_1_n0[4]), .N5(n8bitwisexor_1_n0[5]), .N6(n8bitwisexor_1_n0[6]), .N7(n8bitwisexor_1_n0[7]));
  _8bitwiseXNOR u_8bitwisexnor_1 (
    .A0(A[0]), .B0(B[0]), .A1(A[1]), .B1(B[1]), .A2(A[2]), .B2(B[2]), .A3(A[3]), .B3(B[3]), .A4(A[4]),
    .B4(B[4]), .A5(A[5]), .B5(B[5]), .A6(A[6]), .B6(B[6]), .A7(A[7]), .B7(B[7]), .N0(n8bitwisexnor_1_n0[0]),
    .N1(n8bitwisexnor_1_n0[1]), .N2(n8bitwisexnor_1_n0[2]), .N3(n8bitwisexnor_1_n0[3]),
    .N4(n8bitwisexnor_1_n0[4]), .N5(n8bitwisexnor_1_n0[5]), .N6(n8bitwisexnor_1_n0[6]),
    .N7(n8bitwisexnor_1_n0[7]));
  xor xor_1 (xor_1_out, and_1_out, sub);
  xor xor_2 (xor_2_out, and_2_out, sub);
  xor xor_3 (xor_3_out, and_3_out, sub);
  xor xor_4 (xor_4_out, and_4_out, sub);
  xor xor_5 (xor_5_out, and_5_out, sub);
  xor xor_6 (xor_6_out, and_6_out, sub);
  xor xor_7 (xor_7_out, and_7_out, sub);
  xor xor_8 (xor_8_out, and_8_out, sub);
  _8bit_full_adder u_8bit_full_adder_1 (
    .A2(A[2]), .A0(A[0]), .A1(A[1]), .B2(xor_3_out), .B0(xor_1_out), .B1(xor_2_out), .A3(A[3]), .A4(A[4]),
    .A5(A[5]), .A6(A[6]), .A7(A[7]), .B3(xor_4_out), .B4(xor_5_out), .B5(xor_6_out), .B6(xor_7_out),
    .B7(xor_8_out), .COUT(cout), .S7(n8bit_full_adder_1_s0[7]), .S5(n8bit_full_adder_1_s0[5]),
    .S6(n8bit_full_adder_1_s0[6]), .S0(n8bit_full_adder_1_s0[0]), .S1(n8bit_full_adder_1_s0[1]),
    .S2(n8bit_full_adder_1_s0[2]), .S3(n8bit_full_adder_1_s0[3]), .S4(n8bit_full_adder_1_s0[4]), .cin(cin));
  _8_to_one_mux u_8_to_one_mux_1 (
    ._2(n8bit_multiplier_1_m0), ._1(n8bit_full_adder_1_s0), ._4(n8bitwisenand_1_n0), ._3(n8bitwiseand_1_n0),
    ._6(n8bitwisenor_1_n0), ._5(n8bitwiseor_1_n0), ._8(n8bitwisexnor_1_n0), ._7(n8bitwisexor_1_n0),
    .out(OUTPUT), .s0(S0), .s1(S1), .s2(S2));
endmodule

module _8bitwiseAND (
  input  A0,
  input  B0,
  input  A1,
  input  B1,
  input  A2,
  input  B2,
  input  A3,
  input  B3,
  input  A4,
  input  B4,
  input  A5,
  input  B5,
  input  A6,
  input  B6,
  input  A7,
  input  B7,
  output N0,
  output N1,
  output N2,
  output N3,
  output N4,
  output N5,
  output N6,
  output N7
);

  and and_1 (N0, A0, B0);
  and and_2 (N6, A6, B6);
  and and_3 (N1, A1, B1);
  and and_4 (N2, A2, B2);
  and and_5 (N3, A3, B3);
  and and_6 (N4, A4, B4);
  and and_7 (N5, A5, B5);
  and and_8 (N7, A7, B7);
endmodule

module _8bitwiseNAND (
  input  A0,
  input  B0,
  input  A1,
  input  B1,
  input  A2,
  input  B2,
  input  A3,
  input  B3,
  input  A4,
  input  B4,
  input  A5,
  input  B5,
  input  A6,
  input  B6,
  input  A7,
  input  B7,
  output N0,
  output N1,
  output N2,
  output N3,
  output N4,
  output N5,
  output N6,
  output N7
);

  nand nand_1 (N6, A6, B6);
  nand nand_2 (N0, A0, B0);
  nand nand_3 (N1, A1, B1);
  nand nand_4 (N2, A2, B2);
  nand nand_5 (N3, A3, B3);
  nand nand_6 (N4, A4, B4);
  nand nand_7 (N5, A5, B5);
  nand nand_8 (N7, A7, B7);
endmodule

module _8bitwiseOR (
  input  A0,
  input  B0,
  input  A1,
  input  B1,
  input  A2,
  input  B2,
  input  A3,
  input  B3,
  input  A4,
  input  B4,
  input  A5,
  input  B5,
  input  A6,
  input  B6,
  input  A7,
  input  B7,
  output N0,
  output N1,
  output N2,
  output N3,
  output N4,
  output N5,
  output N6,
  output N7
);

  or or_1 (N0, A0, B0);
  or or_2 (N6, A6, B6);
  or or_3 (N1, A1, B1);
  or or_4 (N2, A2, B2);
  or or_5 (N3, A3, B3);
  or or_6 (N4, A4, B4);
  or or_7 (N5, A5, B5);
  or or_8 (N7, A7, B7);
endmodule

module _8bitwiseNOR (
  input  A0,
  input  B0,
  input  A1,
  input  B1,
  input  A2,
  input  B2,
  input  A3,
  input  B3,
  input  A4,
  input  B4,
  input  A5,
  input  B5,
  input  A6,
  input  B6,
  input  A7,
  input  B7,
  output N0,
  output N1,
  output N2,
  output N3,
  output N4,
  output N5,
  output N6,
  output N7
);

  nor nor_1 (N6, A6, B6);
  nor nor_2 (N0, A0, B0);
  nor nor_3 (N1, A1, B1);
  nor nor_4 (N2, A2, B2);
  nor nor_5 (N3, A3, B3);
  nor nor_6 (N4, A4, B4);
  nor nor_7 (N5, A5, B5);
  nor nor_8 (N7, A7, B7);
endmodule

module _8bitwiseXOR (
  input  A0,
  input  B0,
  input  A1,
  input  B1,
  input  A2,
  input  B2,
  input  A3,
  input  B3,
  input  A4,
  input  B4,
  input  A5,
  input  B5,
  input  A6,
  input  B6,
  input  A7,
  input  B7,
  output N0,
  output N1,
  output N2,
  output N3,
  output N4,
  output N5,
  output N6,
  output N7
);

  xor xor_1 (N6, A6, B6);
  xor xor_2 (N0, A0, B0);
  xor xor_3 (N1, A1, B1);
  xor xor_4 (N2, A2, B2);
  xor xor_5 (N3, A3, B3);
  xor xor_6 (N4, A4, B4);
  xor xor_7 (N5, A5, B5);
  xor xor_8 (N7, A7, B7);
endmodule

module _8bitwiseXNOR (
  input  A0,
  input  B0,
  input  A1,
  input  B1,
  input  A2,
  input  B2,
  input  A3,
  input  B3,
  input  A4,
  input  B4,
  input  A5,
  input  B5,
  input  A6,
  input  B6,
  input  A7,
  input  B7,
  output N0,
  output N1,
  output N2,
  output N3,
  output N4,
  output N5,
  output N6,
  output N7
);

  xnor xnor_1 (N6, A6, B6);
  xnor xnor_2 (N0, A0, B0);
  xnor xnor_3 (N1, A1, B1);
  xnor xnor_4 (N2, A2, B2);
  xnor xnor_5 (N3, A3, B3);
  xnor xnor_6 (N4, A4, B4);
  xnor xnor_7 (N5, A5, B5);
  xnor xnor_8 (N7, A7, B7);
endmodule

module _8_to_one_mux (
  input  s1,
  input  s2,
  input  s0,
  input  [7:0] _2,
  input  [7:0] _1,
  input  [7:0] _4,
  input  [7:0] _3,
  input  [7:0] _6,
  input  [7:0] _5,
  input  [7:0] _8,
  input  [7:0] _7,
  output [7:0] out
);

  wire [7:0] n2_to_one_mux_1_out0, n2_to_one_mux_2_out0, n2_to_one_mux_3_out0, n2_to_one_mux_4_out0,
       n2_to_one_mux_5_out0, n2_to_one_mux_6_out0;

  _2_to_one_mux u_2_to_one_mux_1 (
    .A0(_1[0]), .B0(_2[0]), .A1(_1[1]), .B1(_2[1]), .A2(_1[2]), .B2(_2[2]), .A3(_1[3]), .B3(_2[3]),
    .A4(_1[4]), .B4(_2[4]), .A5(_1[5]), .B5(_2[5]), .A6(_1[6]), .B6(_2[6]), .A7(_1[7]), .B7(_2[7]),
    .OUT0(n2_to_one_mux_1_out0[0]), .OUT1(n2_to_one_mux_1_out0[1]), .OUT2(n2_to_one_mux_1_out0[2]),
    .OUT3(n2_to_one_mux_1_out0[3]), .OUT4(n2_to_one_mux_1_out0[4]), .OUT5(n2_to_one_mux_1_out0[5]),
    .OUT6(n2_to_one_mux_1_out0[6]), .OUT7(n2_to_one_mux_1_out0[7]), .S(s0));
  _2_to_one_mux u_2_to_one_mux_2 (
    .A0(_3[0]), .B0(_4[0]), .A1(_3[1]), .B1(_4[1]), .A2(_3[2]), .B2(_4[2]), .A3(_3[3]), .B3(_4[3]),
    .A4(_3[4]), .B4(_4[4]), .A5(_3[5]), .B5(_4[5]), .A6(_3[6]), .B6(_4[6]), .A7(_3[7]), .B7(_4[7]),
    .OUT0(n2_to_one_mux_2_out0[0]), .OUT1(n2_to_one_mux_2_out0[1]), .OUT2(n2_to_one_mux_2_out0[2]),
    .OUT3(n2_to_one_mux_2_out0[3]), .OUT4(n2_to_one_mux_2_out0[4]), .OUT5(n2_to_one_mux_2_out0[5]),
    .OUT6(n2_to_one_mux_2_out0[6]), .OUT7(n2_to_one_mux_2_out0[7]), .S(s0));
  _2_to_one_mux u_2_to_one_mux_3 (
    .A0(_5[0]), .B0(_6[0]), .A1(_5[1]), .B1(_6[1]), .A2(_5[2]), .B2(_6[2]), .A3(_5[3]), .B3(_6[3]),
    .A4(_5[4]), .B4(_6[4]), .A5(_5[5]), .B5(_6[5]), .A6(_5[6]), .B6(_6[6]), .A7(_5[7]), .B7(_6[7]),
    .OUT0(n2_to_one_mux_3_out0[0]), .OUT1(n2_to_one_mux_3_out0[1]), .OUT2(n2_to_one_mux_3_out0[2]),
    .OUT3(n2_to_one_mux_3_out0[3]), .OUT4(n2_to_one_mux_3_out0[4]), .OUT5(n2_to_one_mux_3_out0[5]),
    .OUT6(n2_to_one_mux_3_out0[6]), .OUT7(n2_to_one_mux_3_out0[7]), .S(s0));
  _2_to_one_mux u_2_to_one_mux_4 (
    .A0(_7[0]), .B0(_8[0]), .A1(_7[1]), .B1(_8[1]), .A2(_7[2]), .B2(_8[2]), .A3(_7[3]), .B3(_8[3]),
    .A4(_7[4]), .B4(_8[4]), .A5(_7[5]), .B5(_8[5]), .A6(_7[6]), .B6(_8[6]), .A7(_7[7]), .B7(_8[7]),
    .OUT0(n2_to_one_mux_4_out0[0]), .OUT1(n2_to_one_mux_4_out0[1]), .OUT2(n2_to_one_mux_4_out0[2]),
    .OUT3(n2_to_one_mux_4_out0[3]), .OUT4(n2_to_one_mux_4_out0[4]), .OUT5(n2_to_one_mux_4_out0[5]),
    .OUT6(n2_to_one_mux_4_out0[6]), .OUT7(n2_to_one_mux_4_out0[7]), .S(s0));
  _2_to_one_mux u_2_to_one_mux_5 (
    .A0(n2_to_one_mux_1_out0[0]), .B0(n2_to_one_mux_2_out0[0]), .A1(n2_to_one_mux_1_out0[1]),
    .B1(n2_to_one_mux_2_out0[1]), .A2(n2_to_one_mux_1_out0[2]), .B2(n2_to_one_mux_2_out0[2]),
    .A3(n2_to_one_mux_1_out0[3]), .B3(n2_to_one_mux_2_out0[3]), .A4(n2_to_one_mux_1_out0[4]),
    .B4(n2_to_one_mux_2_out0[4]), .A5(n2_to_one_mux_1_out0[5]), .B5(n2_to_one_mux_2_out0[5]),
    .A6(n2_to_one_mux_1_out0[6]), .B6(n2_to_one_mux_2_out0[6]), .A7(n2_to_one_mux_1_out0[7]),
    .B7(n2_to_one_mux_2_out0[7]), .OUT0(n2_to_one_mux_5_out0[0]), .OUT1(n2_to_one_mux_5_out0[1]),
    .OUT2(n2_to_one_mux_5_out0[2]), .OUT3(n2_to_one_mux_5_out0[3]), .OUT4(n2_to_one_mux_5_out0[4]),
    .OUT5(n2_to_one_mux_5_out0[5]), .OUT6(n2_to_one_mux_5_out0[6]), .OUT7(n2_to_one_mux_5_out0[7]), .S(s1));
  _2_to_one_mux u_2_to_one_mux_6 (
    .A0(n2_to_one_mux_3_out0[0]), .B0(n2_to_one_mux_4_out0[0]), .A1(n2_to_one_mux_3_out0[1]),
    .B1(n2_to_one_mux_4_out0[1]), .A2(n2_to_one_mux_3_out0[2]), .B2(n2_to_one_mux_4_out0[2]),
    .A3(n2_to_one_mux_3_out0[3]), .B3(n2_to_one_mux_4_out0[3]), .A4(n2_to_one_mux_3_out0[4]),
    .B4(n2_to_one_mux_4_out0[4]), .A5(n2_to_one_mux_3_out0[5]), .B5(n2_to_one_mux_4_out0[5]),
    .A6(n2_to_one_mux_3_out0[6]), .B6(n2_to_one_mux_4_out0[6]), .A7(n2_to_one_mux_3_out0[7]),
    .B7(n2_to_one_mux_4_out0[7]), .OUT0(n2_to_one_mux_6_out0[0]), .OUT1(n2_to_one_mux_6_out0[1]),
    .OUT2(n2_to_one_mux_6_out0[2]), .OUT3(n2_to_one_mux_6_out0[3]), .OUT4(n2_to_one_mux_6_out0[4]),
    .OUT5(n2_to_one_mux_6_out0[5]), .OUT6(n2_to_one_mux_6_out0[6]), .OUT7(n2_to_one_mux_6_out0[7]), .S(s1));
  _2_to_one_mux u_2_to_one_mux_7 (
    .A0(n2_to_one_mux_5_out0[0]), .B0(n2_to_one_mux_6_out0[0]), .A1(n2_to_one_mux_5_out0[1]),
    .B1(n2_to_one_mux_6_out0[1]), .A2(n2_to_one_mux_5_out0[2]), .B2(n2_to_one_mux_6_out0[2]),
    .A3(n2_to_one_mux_5_out0[3]), .B3(n2_to_one_mux_6_out0[3]), .A4(n2_to_one_mux_5_out0[4]),
    .B4(n2_to_one_mux_6_out0[4]), .A5(n2_to_one_mux_5_out0[5]), .B5(n2_to_one_mux_6_out0[5]),
    .A6(n2_to_one_mux_5_out0[6]), .B6(n2_to_one_mux_6_out0[6]), .A7(n2_to_one_mux_5_out0[7]),
    .B7(n2_to_one_mux_6_out0[7]), .OUT0(out[0]), .OUT1(out[1]), .OUT2(out[2]), .OUT3(out[3]), .OUT4(out[4]),
    .OUT5(out[5]), .OUT6(out[6]), .OUT7(out[7]), .S(s2));
endmodule

module _2_to_one_mux (
  input  A0,
  input  B0,
  input  A1,
  input  B1,
  input  A2,
  input  B2,
  input  A3,
  input  B3,
  input  A4,
  input  B4,
  input  A5,
  input  B5,
  input  A6,
  input  B6,
  input  A7,
  input  B7,
  input  S,
  output OUT0,
  output OUT1,
  output OUT2,
  output OUT3,
  output OUT4,
  output OUT5,
  output OUT6,
  output OUT7
);

  wire and_1_out, and_2_out, and_3_out, and_4_out, and_5_out, and_6_out, and_7_out, and_8_out, and_9_out,
       and_10_out, and_11_out, and_12_out, and_13_out, and_14_out, and_15_out, and_16_out, not_1_out,
       not_2_out, not_3_out, not_4_out, not_5_out, not_6_out, not_7_out, not_8_out;

  not not_1 (not_1_out, S);
  not not_2 (not_2_out, S);
  not not_3 (not_3_out, S);
  not not_4 (not_4_out, S);
  not not_5 (not_5_out, S);
  not not_6 (not_6_out, S);
  not not_7 (not_7_out, S);
  not not_8 (not_8_out, S);
  and and_1 (and_1_out, A3, not_1_out);
  and and_2 (and_2_out, B3, S);
  and and_3 (and_3_out, A4, not_2_out);
  and and_4 (and_4_out, B4, S);
  and and_5 (and_5_out, A5, not_3_out);
  and and_6 (and_6_out, B5, S);
  and and_7 (and_7_out, A6, not_4_out);
  and and_8 (and_8_out, B6, S);
  and and_9 (and_9_out, A7, not_5_out);
  and and_10 (and_10_out, B7, S);
  and and_11 (and_11_out, A0, not_6_out);
  and and_12 (and_12_out, B0, S);
  and and_13 (and_13_out, A1, not_7_out);
  and and_14 (and_14_out, B1, S);
  and and_15 (and_15_out, A2, not_8_out);
  and and_16 (and_16_out, B2, S);
  or or_1 (OUT4, and_3_out, and_4_out);
  or or_2 (OUT5, and_5_out, and_6_out);
  or or_3 (OUT6, and_7_out, and_8_out);
  or or_4 (OUT7, and_9_out, and_10_out);
  or or_5 (OUT0, and_11_out, and_12_out);
  or or_6 (OUT1, and_13_out, and_14_out);
  or or_7 (OUT2, and_15_out, and_16_out);
  or or_8 (OUT3, and_1_out, and_2_out);
endmodule

module DDA_new (
  input  in3,
  input  in2,
  input  in1,
  input  in0,
  output out3,
  output out2,
  output out1,
  output out0
);

  wire and_1_out, and_2_out, and_3_out, and_4_out, and_5_out, and_6_out, and_7_out, and_8_out, and_9_out,
       and_10_out, and_11_out, not_1_out, not_2_out, not_3_out, not_4_out, not_5_out, not_6_out, not_7_out,
       not_8_out, not_9_out, not_10_out;

  and and_1 (and_1_out, in2, in0);
  and and_2 (and_2_out, in2, in1);
  not not_1 (not_1_out, in1);
  and and_3 (and_3_out, in2, not_1_out, not_2_out);
  not not_2 (not_2_out, in0);
  and and_4 (and_4_out, in3, in0);
  and and_5 (and_5_out, in3, in1);
  not not_3 (not_3_out, in3);
  and and_6 (and_6_out, not_3_out, not_4_out, in1);
  not not_4 (not_4_out, in2);
  and and_7 (and_7_out, in1, in0);
  and and_8 (and_8_out, in3, not_5_out, not_6_out);
  not not_5 (not_5_out, in1);
  not not_6 (not_6_out, in0);
  not not_7 (not_7_out, in3);
  and and_9 (and_9_out, not_7_out, not_8_out, in0);
  not not_8 (not_8_out, in2);
  and and_10 (and_10_out, in2, in1, not_9_out);
  not not_9 (not_9_out, in0);
  and and_11 (and_11_out, in3, not_10_out);
  not not_10 (not_10_out, in0);
  or or_1 (out3, and_1_out, and_2_out, in3);
  or or_2 (out2, and_3_out, and_4_out, and_5_out);
  or or_3 (out1, and_6_out, and_7_out, and_8_out);
  or or_4 (out0, and_9_out, and_10_out, and_11_out);
endmodule

module DDA_ALGORITHM (
  input  [7:0] \input ,
  output [3:0] hundreds,
  output [3:0] tens,
  output [3:0] ones
);

  wire dda_new_1_out0, dda_new_1_out1, dda_new_1_out2, dda_new_1_out3, dda_new_2_out0, dda_new_2_out1,
       dda_new_2_out2, dda_new_2_out3, dda_new_3_out0, dda_new_3_out1, dda_new_3_out2, dda_new_3_out3,
       dda_new_4_out0, dda_new_4_out1, dda_new_4_out2, dda_new_6_out0, dda_new_6_out1, dda_new_6_out2,
       dda_new_6_out3;

  DDA_new dda_new_1 (
    .in3(1'b0), .in2(\input [7]), .in1(\input [6]), .in0(\input [5]), .out3(dda_new_1_out3),
    .out2(dda_new_1_out2), .out1(dda_new_1_out1), .out0(dda_new_1_out0));
  DDA_new dda_new_2 (
    .in3(dda_new_1_out2), .in2(dda_new_1_out1), .in1(dda_new_1_out0), .in0(\input [4]),
    .out3(dda_new_2_out3), .out2(dda_new_2_out2), .out1(dda_new_2_out1), .out0(dda_new_2_out0));
  DDA_new dda_new_3 (
    .in3(dda_new_2_out2), .in2(dda_new_2_out1), .in1(dda_new_2_out0), .in0(\input [3]),
    .out3(dda_new_3_out3), .out2(dda_new_3_out2), .out1(dda_new_3_out1), .out0(dda_new_3_out0));
  DDA_new dda_new_4 (
    .in3(1'b0), .in2(dda_new_1_out3), .in1(dda_new_2_out3), .in0(dda_new_3_out3), .out3(hundreds[1]),
    .out2(dda_new_4_out2), .out1(dda_new_4_out1), .out0(dda_new_4_out0));
  DDA_new dda_new_5 (
    .in3(dda_new_4_out2), .in2(dda_new_4_out1), .in1(dda_new_4_out0), .in0(dda_new_6_out3),
    .out3(hundreds[0]), .out2(tens[3]), .out1(tens[2]), .out0(tens[1]));
  DDA_new dda_new_6 (
    .in3(dda_new_3_out2), .in2(dda_new_3_out1), .in1(dda_new_3_out0), .in0(\input [2]),
    .out3(dda_new_6_out3), .out2(dda_new_6_out2), .out1(dda_new_6_out1), .out0(dda_new_6_out0));
  DDA_new dda_new_7 (
    .in3(dda_new_6_out2), .in2(dda_new_6_out1), .in1(dda_new_6_out0), .in0(\input [1]), .out3(tens[0]),
    .out2(ones[3]), .out1(ones[2]), .out0(ones[1]));

  assign hundreds[3:2] = 2'b00;
  assign ones[0] = \input [0];
endmodule

module BCD_TO_7SEGMENT_new1 (
  input  a3,
  input  a2,
  input  a1,
  input  a12,
  output a,
  output b,
  output c,
  output d,
  output e,
  output f,
  output g
);

  wire and_1_out, and_2_out, and_3_out, and_4_out, and_5_out, and_6_out, and_7_out, and_8_out, and_9_out,
       and_10_out, and_11_out, and_12_out, and_13_out, and_14_out, and_15_out, and_16_out, and_17_out,
       not_1_out, not_2_out, not_3_out, not_4_out, not_5_out, not_6_out, not_7_out, not_8_out, not_9_out,
       not_10_out, not_11_out, not_12_out, not_13_out, not_14_out, not_15_out, not_16_out, not_17_out,
       not_18_out, not_19_out, not_20_out, not_21_out, or_1_out, or_2_out, or_3_out, or_4_out, or_6_out,
       or_8_out, or_9_out, or_10_out, or_11_out, or_14_out, or_15_out;

  not not_1 (not_1_out, a2);
  and and_1 (and_1_out, not_1_out, not_2_out);
  not not_2 (not_2_out, a12);
  and and_2 (and_2_out, a2, a12);
  not not_3 (not_3_out, a2);
  not not_4 (not_4_out, a1);
  and and_3 (and_3_out, not_4_out, not_5_out);
  not not_5 (not_5_out, a12);
  not not_6 (not_6_out, a1);
  or or_1 (or_1_out, not_6_out, a12);
  not not_7 (not_7_out, a2);
  and and_4 (and_4_out, not_7_out, not_8_out);
  not not_8 (not_8_out, a12);
  not not_9 (not_9_out, a2);
  and and_5 (and_5_out, not_9_out, a1);
  not not_10 (not_10_out, a12);
  and and_6 (and_6_out, a2, not_11_out);
  not not_11 (not_11_out, a1);
  not not_12 (not_12_out, a2);
  and and_7 (and_7_out, not_12_out, not_13_out);
  not not_13 (not_13_out, a12);
  and and_8 (and_8_out, a1, not_14_out);
  not not_14 (not_14_out, a12);
  not not_15 (not_15_out, a1);
  and and_9 (and_9_out, not_15_out, not_16_out);
  not not_16 (not_16_out, a12);
  and and_10 (and_10_out, a2, not_17_out);
  not not_17 (not_17_out, a1);
  and and_11 (and_11_out, a2, not_18_out);
  not not_18 (not_18_out, a12);
  not not_19 (not_19_out, a2);
  and and_12 (and_12_out, not_19_out, a1);
  and and_13 (and_13_out, a2, not_20_out);
  not not_20 (not_20_out, a1);
  and and_14 (and_14_out, a2, not_21_out);
  not not_21 (not_21_out, a12);
  or or_2 (or_2_out, and_1_out, a1);
  or or_3 (or_3_out, and_2_out, a3);
  or or_4 (or_4_out, not_3_out, and_3_out);
  and and_15 (and_15_out, a1, a12);
  or or_5 (c, or_1_out, a2);
  or or_6 (or_6_out, and_4_out, and_5_out);
  and and_16 (and_16_out, a1, not_10_out);
  and and_17 (and_17_out, and_6_out, a12);
  or or_7 (e, and_7_out, and_8_out);
  or or_8 (or_8_out, and_9_out, and_10_out);
  or or_9 (or_9_out, and_11_out, a3);
  or or_10 (or_10_out, and_12_out, and_13_out);
  or or_11 (or_11_out, and_14_out, a3);
  or or_12 (a, or_2_out, or_3_out);
  or or_13 (b, or_4_out, and_15_out);
  or or_14 (or_14_out, or_6_out, and_16_out);
  or or_15 (or_15_out, and_17_out, a3);
  or or_16 (f, or_8_out, or_9_out);
  or or_17 (g, or_10_out, or_11_out);
  or or_18 (d, or_14_out, or_15_out);
endmodule
